# Fritzing sketch valv-solenoide (saved by Fritzing 0.9.3b)
breadboards: 1

parts:
  R1 = TRIMPOT [package=trimpot_pth_s3_lock]
  Part1 = Arduino Uno (Rev3)
  R2 = Resistor [tolerance=±5% resistance=220 package="1206 [SMD]"]
  Q1 = NPN-Transistor [package="TO92 [THT]"]
  D1 = Zener Diode [part_number=1N4732A breakdown_voltage=3.6V package="300 mil [THT]"]
  L1 = Solenoid

nets:
  N1: R1.CCW, Part1.5V, D1.cathode, L1.pin2
  N2: R1.WIPER, Part1.A1
  N3: R1.CW, Part1.GND, Q1.C
  N4: Part1.D13/SCK, R2.Pin_1
  N5: R2.Pin_0, Q1.B
  N6: Q1.E, D1.anode, L1.pin1

// code stored in the sketch: solenoid blink.ino
/*
  solenoid blink
*/

const int pin=13;
int deltime=1000;

// the setup function runs once when you press reset or power the board
void setup() {
  // initialize digital pin LED_BUILTIN as an output.
  pinMode(pin, OUTPUT);
}

// the loop function runs over and over again forever
void loop() {
  deltime=analogRead(1);
  digitalWrite(pin, HIGH);   // turn the LED on (HIGH is the voltage level)
  delay(60);                       // wait for a second
  digitalWrite(pin, LOW);    // turn the LED off by making the voltage LOW
  delay(deltime);                       // wait for a second
}
